# Fritzing sketch Pegboard (saved by Fritzing 0.9.3b)
breadboards: 3
stripboards: 2

parts:
  Part1 = Arduino Uno (Rev3)
  Raspberry_Pi_1 = Raspberry Pi 3 [part_number=RPI-3-V1.2]  # not connected
  Raspberry_Pi_Zero1 = Raspberry Pi Zero  # not connected
  RELAY1 = CAR RELAY [part_number=NVF4-2 package=THT]  # not connected
  RELAY2 = CAR RELAY [part_number=NVF4-2 package=THT]  # not connected
  J2 = female pin header, 2 pins [form="♀ (female)"]  # not connected
  J3 = female pin header, 2 pins [form="♀ (female)"]  # not connected
  S1 = Round Pushbutton  # not connected
  LED1 = SMD RGB LED (WS2812) [package=5050]  # not connected
  LED3 = SMD RGB LED (WS2812) [package=5050]  # not connected
  LED4 = SMD RGB LED (WS2812) [package=5050]  # not connected
  LED5 = SMD RGB LED (WS2812) [package=5050]  # not connected
  LED6 = SMD RGB LED (WS2812) [package=5050]  # not connected
  LED7 = SMD RGB LED (WS2812) [package=5050]  # not connected
  LED8 = SMD RGB LED (WS2812) [package=5050]  # not connected
  LED9 = SMD RGB LED (WS2812) [package=5050]  # not connected
  LED10 = SMD RGB LED (WS2812) [package=5050]  # not connected
  LED11 = SMD RGB LED (WS2812) [package=5050]  # not connected
  LED13 = SMD RGB LED (WS2812) [package=5050]  # not connected
  S2 = Round Pushbutton  # not connected
  S3 = Round Pushbutton  # not connected
  S4 = Round Pushbutton  # not connected
  M1 = Niren can bus module [package=THT]
  LED14 = smd LED [color="Yellow (595nm)" package="0603 [SMD]"]  # not connected
  LED15 = smd LED [color="Yellow (595nm)" package="0603 [SMD]"]  # not connected
  OMRON1 = OMRON PCB Power Relay – G5LE [part_number="G5LE-1\n" package=THT]  # not connected
  LED12 = SMD RGB LED (WS2812) [package=5050]  # not connected
  R2 = Resistor [tolerance=±5% resistance=116k package=THT]  # not connected
  R1 = Resistor [tolerance=±5% resistance=116k package=THT]  # not connected
  R4 = Resistor [tolerance=±5% resistance=22k package=THT]
  R3 = Resistor [tolerance=±5% resistance=48k package=THT]
  R5 = Resistor [tolerance=±5% resistance=48k package=THT]
  R6 = Resistor [tolerance=±5% resistance=22k package=THT]
  R7 = Resistor [tolerance=±5% resistance=22k package=THT]
  R8 = Resistor [tolerance=±5% resistance=48k package=THT]
  R9 = Resistor [tolerance=±5% resistance=22k package=THT]
  R10 = Resistor [tolerance=±5% resistance=48k package=THT]
  F2 = FUSE [package=fuse_5mm]
  F3 = FUSE [package=fuse_5mm]
  F4 = FUSE [package=fuse_5mm]
  F5 = FUSE [package=fuse_5mm]
  F6 = FUSE [package=fuse_5mm]
  F7 = FUSE [package=fuse_5mm]
  J4 = female pin header, 2 pins [form="♀ (female)"]
  LED16 = SMD RGB LED (WS2812) [package=5050]  # not connected
  LED17 = SMD RGB LED (WS2812) [package=5050]  # not connected
  LED18 = SMD RGB LED (WS2812) [package=5050]  # not connected
  LED19 = SMD RGB LED (WS2812) [package=5050]  # not connected
  LED20 = SMD RGB LED (WS2812) [package=5050]  # not connected
  LED21 = SMD RGB LED (WS2812) [package=5050]  # not connected

nets:
  N1: Part1.D10_PWM/SS, M1.pin3
  N2: Part1.D11_PWM/MOSI, M1.pin5
  N3: Part1.D12/MISO, M1.pin4
  N4: Part1.D13/SCK, M1.pin6
  N5: R4.Pin_0, R3.Pin_0
  N6: R4.Pin_1, R6.Pin_1, R7.Pin_1, R9.Pin_1
  N7: R5.Pin_0, R6.Pin_0
  N8: R7.Pin_0, R8.Pin_0
  N9: R9.Pin_0, R10.Pin_0
  N10: F2.2, F3.2, F4.2, F5.2, F6.2, F7.2, J4.pin1

notes:
  TB 2
  1
  2
  3
  4
  PiCAN Hat
  +12V
  GND
  CAN_L
  CAN_H
  R2
  R1
  a
  b
  SB-R
  SB-L
  SB-HZ
  SB-HL
  LCU 2
  LCU 1
  Flasher 1
  Flasher 2
  R3
  R6
  R8
  R10
  R7
  R9
  R5
  R4
  LED-L
  LED-R
  LED-HL
  5
  6
  Primary Fuse Box
  LED-HZ
  hello

custom parts:
  Niren can bus module: Niren can bus module availabe on ebay and others. No pcb view as no mechanical drawng and it wouldn't mount anyway.
